# Fritzing sketch Jingle_Bells (saved by Fritzing 0.9.4)
breadboards: 1

parts:
  Part1 = Arduino Uno (Rev3)
  LED1 = RGB LED (com. cathode, rgb) [package="5 mm [THT]"]
  R1 = Resistor [tolerance=±5% resistance=470 package=THT]
  R2 = Resistor [tolerance=±5% resistance=470 package=THT]
  R3 = Resistor [tolerance=±5% resistance=470 package=THT]
  J1 = Piezo Speaker

nets:
  N1: Part1.D9_PWM, R1.Pin_1
  N2: Part1.GND, J1.pin1
  N3: Part1.D3_PWM, J1.pin2
  N4: Part1.D5_PWM, R3.Pin_1
  N5: Part1.D6_PWM, R2.Pin_1
  N6: LED1.red_anode, R1.Pin_0
  N7: LED1.green_anode, R2.Pin_0
  N8: LED1.blue_anode, R3.Pin_0
